# Fritzing sketch morsecode doorlock (saved by Fritzing 0.9.3b)
breadboards: 1

parts:
  Part1 = Arduino Uno (Rev3)
  LED1 = LED - 5mm [color="Red (633nm)" package="5 mm [THT]"]
  R1 = Photocell (LDR) [package=THT]
  R3 = TRIMPOT [package=trimpot_pth_s3_lock]
  J1 = Piezo Speaker
  R4 = Resistor [tolerance=±5% resistance=220 package=THT]
  R5 = Resistor [tolerance=±5% resistance=220 package=THT]
  J2 = Basic Servo

nets:
  N1: Part1.A2, R3.WIPER
  N2: Part1.A3, R1.pin_0, R5.Pin_1
  N3: Part1.D8, R4.Pin_0
  N4: Part1.D9_PWM, J2.pulse
  N5: Part1.D10_PWM/SS, J1.pin2
  GND: Part1.GND, LED1.anode, R3.CCW, R5.Pin_0, J2.gnd
  N6: Part1.5V, R1.pin_1, R3.CW
  N7: LED1.cathode, R4.Pin_1
